# Fritzing sketch P3 (saved by Fritzing 0.9.3b)
breadboards: 1

parts:
  U1 = NodeMCU V1.0
  Part1 = RFID-RC522-v3
  IR = TSOP312.., 314.. [package=THT]
  LED1 = RGB LED (com. cathode, rgb) [package="5 mm [THT]"]
  R4 = Resistor Mini [tolerance=±5% resistance=220 package=THT]
  R5 = Resistor Mini [tolerance=±5% resistance=220 package=THT]
  R7 = Resistor Mini [tolerance=±5% resistance=220 package=THT]
  J1 = Piezo Speaker

nets (from the schematic view):
  N1: U1.D0, J1.pin2
  N2: U1.D1, IR.Data
  N3: U1.D2, R4.Pin_1
  N4: U1.D3, R5.Pin_1
  N5: U1.D4, Part1.SDA
  3V3: U1.3V3, Part1.3.3V, IR.Vs
  GND: U1.GND, Part1.GND, IR.GND, LED1.common_cathode, J1.pin1
  N6: U1.D5, Part1.SCK
  N7: U1.D6, Part1.MISO
  N8: U1.D7, Part1.MOSI
  N9: U1.D8, R7.Pin_1

custom parts:
  NodeMCU V1.0: ESP8266 based NodeMCU
  RFID-RC522-v3: A simple China made RFID-RC522 Reader (6x4 cm); do check the pin labels, as this is a MFRC522 based clone.
  Resistor Mini: A generic resistor (0.25W)
